# Fritzing sketch l298_driver_arduino (saved by Fritzing 0.9.4)

parts:
  S1 = H-Bridge with L298N
  Part1 = Arduino Mega ADK (Rev3)
  M1 = DC Motor
  M2 = DC Motor
  VCC1 = Battery block 9V
  S2 = H-Bridge with L298N
  M3 = DC Motor
  M4 = DC Motor
  VCC2 = Battery block 9V

nets:
  N1: S1.12V, VCC1.+
  GND: S1.GND, Part1.GND, VCC1.-, S2.GND, VCC2.-
  5V: S1.5V, Part1.5V, S2.5V
  N2: S1.ENA, Part1.D3_PWM
  N3: S1.IN1, Part1.D31
  N4: S1.IN2, Part1.D33
  N5: S1.IN3, Part1.D35
  N6: S1.IN4, Part1.D37
  N7: S1.ENB, Part1.D2_PWM
  N8: S1.M1-01, M2.pin_2
  N9: S1.M1-02, M2.pin_1
  N10: S1.M2-01, M1.pin_2
  N11: S1.M2-02, M1.pin_1
  N12: Part1.D9_PWM, S2.ENB
  N13: Part1.D8_PWM, S2.ENA
  N14: Part1.D43, S2.IN1
  N15: Part1.D45, S2.IN2
  N16: Part1.D47, S2.IN3
  N17: Part1.D49, S2.IN4
  N18: S2.12V, VCC2.+
  N19: S2.M1-01, M4.pin_2
  N20: S2.M1-02, M4.pin_1
  N21: S2.M2-01, M3.pin_2
  N22: S2.M2-02, M3.pin_1

notes:
  4 wheel drive based on Arduino Mega 2560 and L298 Motor Driver
  Code and Schematic by muzzamil21

custom parts:
  H-Bridge with L298N: h-bridge
